// Digital circuit 4Bit_Ram_Module.dig as structural Verilog
module _4Bit_Ram_Module (
  input  R_W,
  input  [3:0] Adrs,
  input  [3:0] D_in,
  input  Clr,
  input  Load,
  output [3:0] D_out
);

  wire and_1_out, and_2_out, and_3_out, and_4_out, and_5_out, and_6_out, and_7_out, and_8_out, and_9_out,
       and_10_out, and_11_out, and_12_out, and_13_out, and_14_out, and_15_out, and_16_out, decoder_1_out_0,
       decoder_1_out_1, decoder_1_out_2, decoder_1_out_3, decoder_1_out_4, decoder_1_out_5, decoder_1_out_6,
       decoder_1_out_7, decoder_1_out_8, decoder_1_out_9, decoder_1_out_10, decoder_1_out_11,
       decoder_1_out_12, decoder_1_out_13, decoder_1_out_14, decoder_1_out_15;
  wire [3:0] _0_q, _1_q, _2_q, _3_q, _4_q, _5_q, _6_q, _7_q, _8_q, _9_q, _10_q, _11_q, _12_q, _13_q, _14_q,
       _15_q;

  Decoder #(.Selector_Bits(4)) decoder_1 (
    .sel(Adrs), .out_0(decoder_1_out_0), .out_1(decoder_1_out_1), .out_2(decoder_1_out_2),
    .out_3(decoder_1_out_3), .out_4(decoder_1_out_4), .out_5(decoder_1_out_5), .out_6(decoder_1_out_6),
    .out_7(decoder_1_out_7), .out_8(decoder_1_out_8), .out_9(decoder_1_out_9), .out_10(decoder_1_out_10),
    .out_11(decoder_1_out_11), .out_12(decoder_1_out_12), .out_13(decoder_1_out_13),
    .out_14(decoder_1_out_14), .out_15(decoder_1_out_15));
  and and_1 (and_1_out, decoder_1_out_0, R_W);
  and and_2 (and_2_out, decoder_1_out_1, R_W);
  and and_3 (and_3_out, decoder_1_out_2, R_W);
  and and_4 (and_4_out, decoder_1_out_3, R_W);
  and and_5 (and_5_out, decoder_1_out_4, R_W);
  and and_6 (and_6_out, decoder_1_out_5, R_W);
  and and_7 (and_7_out, decoder_1_out_6, R_W);
  and and_8 (and_8_out, decoder_1_out_7, R_W);
  and and_9 (and_9_out, decoder_1_out_8, R_W);
  and and_10 (and_10_out, decoder_1_out_9, R_W);
  and and_11 (and_11_out, decoder_1_out_10, R_W);
  and and_12 (and_12_out, decoder_1_out_11, R_W);
  and and_13 (and_13_out, decoder_1_out_12, R_W);
  and and_14 (and_14_out, decoder_1_out_13, R_W);
  and and_15 (and_15_out, decoder_1_out_14, R_W);
  and and_16 (and_16_out, decoder_1_out_15, R_W);
  _4bit_register _0 (.In(D_in), .K(and_1_out), .Clr(Clr), .Load(Load), .Q(_0_q));  // open: Q_2
  _4bit_register _1 (.In(D_in), .K(and_2_out), .Clr(Clr), .Load(Load), .Q(_1_q));  // open: Q_2
  _4bit_register _2 (.In(D_in), .K(and_3_out), .Clr(Clr), .Load(Load), .Q(_2_q));  // open: Q_2
  _4bit_register _3 (.In(D_in), .K(and_4_out), .Clr(Clr), .Load(Load), .Q(_3_q));  // open: Q_2
  _4bit_register _4 (.In(D_in), .K(and_5_out), .Clr(Clr), .Load(Load), .Q(_4_q));  // open: Q_2
  _4bit_register _5 (.In(D_in), .K(and_6_out), .Clr(Clr), .Load(Load), .Q(_5_q));  // open: Q_2
  _4bit_register _6 (.In(D_in), .K(and_7_out), .Clr(Clr), .Load(Load), .Q(_6_q));  // open: Q_2
  _4bit_register _7 (.In(D_in), .K(and_8_out), .Clr(Clr), .Load(Load), .Q(_7_q));  // open: Q_2
  _4bit_register _8 (.In(D_in), .K(and_9_out), .Clr(Clr), .Load(Load), .Q(_8_q));  // open: Q_2
  _4bit_register _9 (.In(D_in), .K(and_10_out), .Clr(Clr), .Load(Load), .Q(_9_q));  // open: Q_2
  _4bit_register _10 (.In(D_in), .K(and_11_out), .Clr(Clr), .Load(Load), .Q(_10_q));  // open: Q_2
  _4bit_register _11 (.In(D_in), .K(and_12_out), .Clr(Clr), .Load(Load), .Q(_11_q));  // open: Q_2
  _4bit_register _12 (.In(D_in), .K(and_13_out), .Clr(Clr), .Load(Load), .Q(_12_q));  // open: Q_2
  _4bit_register _13 (.In(D_in), .K(and_14_out), .Clr(Clr), .Load(Load), .Q(_13_q));  // open: Q_2
  _4bit_register _14 (.In(D_in), .K(and_15_out), .Clr(Clr), .Load(Load), .Q(_14_q));  // open: Q_2
  _4bit_register _15 (.In(D_in), .K(and_16_out), .Clr(Clr), .Load(Load), .Q(_15_q));  // open: Q_2
  Multiplexer #(.Selector_Bits(4), .Bits(4)) multiplexer_1 (
    .sel(Adrs), .in_0(_0_q), .in_1(_1_q), .in_2(_2_q), .in_3(_3_q), .in_4(_4_q), .in_5(_5_q), .in_6(_6_q),
    .in_7(_7_q), .in_8(_8_q), .in_9(_9_q), .in_10(_10_q), .in_11(_11_q), .in_12(_12_q), .in_13(_13_q),
    .in_14(_14_q), .in_15(_15_q), .out(D_out));
endmodule
