// Digital circuit 4bit_ALU.dig as structural Verilog
module _4bit_ALU (
  input  [3:0] A,
  input  [3:0] B,
  input  [2:0] CTRL,
  output [3:0] Out,
  output ZFlg
);

  wire [0:0] slt_1_slt_flag;
  wire [3:0] _4bit_adder_1_sum, _4bit_adder_subractor_1_sum, and_1_out, or_1_out, xor_1_out;

  _4bit_adder _4bit_adder_1 (.C_i__1(1'b0), .A(A), .B(B), .sum(_4bit_adder_1_sum));  // open: C
  _4bit_adder_subractor _4bit_adder_subractor_1 (.K(1'b1), .A(A), .B(B), .sum(_4bit_adder_subractor_1_sum));  // open: C
  assign and_1_out = A & B;  // And and_1, 4 bits wide
  assign or_1_out = A | B;  // Or or_1, 4 bits wide
  assign xor_1_out = A ^ B;  // XOr xor_1, 4 bits wide
  SLT slt_1 (.A(A), .B(B), .SLT_flag(slt_1_slt_flag[0]));
  Multiplexer #(.Selector_Bits(3), .Bits(4)) multiplexer_1 (
    .sel(CTRL), .in_0(_4bit_adder_1_sum), .in_1(_4bit_adder_subractor_1_sum), .in_2(and_1_out),
    .in_3(or_1_out), .in_4(xor_1_out), .in_5({3'b000, slt_1_slt_flag[0]}), .in_6(A), .in_7(B), .out(Out));
  nor nor_1 (ZFlg, Out[0], Out[1], Out[2], Out[3]);
endmodule
