// Digital circuit 4bit_ControlUnit.dig as structural Verilog
module _4bit_ControlUnit (
  input  [3:0] IR,
  input  ZFlg,
  input  K,
  input  Clr,
  input  Fetch,
  output [2:0] ALU_Op,
  output RR1,
  output RR2,
  output WR,
  output WE,
  output IL,
  output PCI,
  output IFE
);

  wire d_ff_5_q, d_ff_6_q, multiplexer_2_out, multiplexer_3_out, multiplexer_4_out,
       write_enable_1_write_enable;
  wire [3:0] d_ff_1_q, multiplexer_1_out;

  Multiplexer #(.Bits(4)) multiplexer_1 (.sel(Clr), .in_0(IR), .in_1(4'b0000), .out(multiplexer_1_out));
  Multiplexer multiplexer_2 (.sel(Clr), .in_0(1'b1), .in_1(1'b0), .out(multiplexer_2_out));
  D_FF d_ff_1 (.D(multiplexer_1_out[0]), .C(K), .Q(d_ff_1_q[0]));  // open: nQ
  D_FF d_ff_2 (.D(multiplexer_1_out[1]), .C(K), .Q(d_ff_1_q[1]));  // open: nQ
  D_FF d_ff_3 (.D(multiplexer_1_out[2]), .C(K), .Q(d_ff_1_q[2]));  // open: nQ
  D_FF d_ff_4 (.D(multiplexer_1_out[3]), .C(K), .Q(d_ff_1_q[3]));  // open: nQ
  Multiplexer multiplexer_3 (.sel(Clr), .in_0(d_ff_5_q), .in_1(1'b0), .out(multiplexer_3_out));
  D_FF d_ff_5 (.D(multiplexer_2_out), .C(K), .Q(d_ff_5_q));  // open: nQ
  Read_Register1 read_register1_1 (.opcode(d_ff_1_q), .read_reg_1(RR1));
  Read_Register2 read_register2_1 (.opcode(d_ff_1_q), .read_reg_2(RR2));
  Write_Register write_register_1 (.opcode(d_ff_1_q), .write_reg(WR));
  Write_Enable write_enable_1 (.opcode(d_ff_1_q), .write_enable(write_enable_1_write_enable));
  Immediate_Load immediate_load_1 (.opcode(d_ff_1_q), .imm_load(IL));
  CU_ALUInstructionMapper cu_aluinstructionmapper_1 (.opcode(d_ff_1_q), .Opp(ALU_Op));
  D_FF d_ff_6 (.D(multiplexer_3_out), .C(K), .Q(d_ff_6_q));  // open: nQ
  and and_1 (WE, write_enable_1_write_enable, Fetch);
  Multiplexer multiplexer_4 (.sel(Clr), .in_0(d_ff_6_q), .in_1(1'b0), .out(multiplexer_4_out));
  D_FF d_ff_7 (.D(multiplexer_4_out), .C(K), .Q(PCI));  // open: nQ

  assign IFE = Fetch;

  // Notes on the sheet:
  //   ALU_Op: ALU Operation
  //   RR1: Read Register 1
  //   RR2: Read Register 2
  //   WR: Write Register
  //   WE: Write Enable
  //   IL: Immediate Load
  //   PCI: PC Increment
  //   IFE: Instruction Fetch Enable
endmodule
