// Digital circuit 4bit_PC.dig as structural Verilog
module _4bit_PC (
  input  [3:0] PC_In,
  input  CTRL,
  input  K,
  input  Clr,
  input  Load,
  input  \new ,
  output [3:0] Out
);

  wire [3:0] _4bit_adder_1_sum, multiplexer_1_out, multiplexer_2_out;

  Multiplexer #(.Bits(4)) multiplexer_1 (.sel(\new ), .in_0(Out), .in_1(PC_In), .out(multiplexer_1_out));
  Multiplexer #(.Bits(4)) multiplexer_2 (
    .sel(CTRL), .in_0(multiplexer_1_out), .in_1(_4bit_adder_1_sum), .out(multiplexer_2_out));
  _4bit_register _4bit_register_1 (.In(multiplexer_2_out), .K(K), .Clr(Clr), .Load(Load), .Q(Out));  // open: Q_2
  _4bit_adder _4bit_adder_1 (.C_i__1(1'b0), .A(Out), .B(4'b0001), .sum(_4bit_adder_1_sum));  // open: C
endmodule
