// Digital circuit 4bit_Processor.dig as structural Verilog
module _4bit_Processor (
  input  Clock,
  input  Clear,
  input  [3:0] Instruction,
  input  State_Transition,
  input  [3:0] IV,
  output [3:0] Output,
  output [3:0] IR_out,
  output [3:0] curr_mem_adrs,
  output [3:0] Ram_out,
  output [3:0] reg_1_out,
  output [3:0] reg_2_out,
  output D,
  output E
);

  wire ALU_zflg, CU_ife, CU_il, CU_pci, CU_rr1, CU_rr2, CU_we, CU_wr, FDE_Cycle_f, not_1_out,
       notconnected_1_out;
  wire [2:0] CU_alu_op;
  wire [3:0] ALU_out;

  FDE_Cycle FDE_Cycle (.In(State_Transition), .K(Clock), .F(FDE_Cycle_f), .D(D), .E(E));
  _4bit_PC PC (
    .PC_In(4'b0000), .CTRL(CU_pci), .K(Clock), .Clr(Clear), .Load(not_1_out), .\new (Clear),
    .Out(curr_mem_adrs));
  _4Bit_Ram_Module RAM (
    .R_W(Clock), .Adrs(curr_mem_adrs), .D_in(Instruction), .Clr(Clear), .Load(not_1_out), .D_out(Ram_out));
  // NotConnected on notconnected_1_out
  _4bit_register IR (.In(Ram_out), .K(Clock), .Clr(Clear), .Load(notconnected_1_out), .Q(IR_out));  // open: Q_2
  not not_1 (not_1_out, CU_ife);
  _4bit_ControlUnit CU (
    .IR(IR_out), .ZFlg(ALU_zflg), .K(Clock), .Clr(Clear), .Fetch(FDE_Cycle_f), .ALU_Op(CU_alu_op),
    .RR1(CU_rr1), .RR2(CU_rr2), .WR(CU_wr), .WE(CU_we), .IL(CU_il), .PCI(CU_pci), .IFE(CU_ife));
  _4bit_RegisterFile RF (
    .RR1(CU_rr1), .RR2(CU_rr2), .WR(CU_wr), .WD(Output), .K(Clock), .WE(CU_we), .Clr(Clear), .RD1(reg_1_out),
    .RD2(reg_2_out));
  _4bit_ALU ALU (.A(reg_1_out), .B(reg_2_out), .CTRL(CU_alu_op), .Out(ALU_out), .ZFlg(ALU_zflg));
  Multiplexer #(.Bits(4)) multiplexer_1 (.sel(CU_il), .in_0(ALU_out), .in_1(IV), .out(Output));

  // Notes on the sheet:
  //   IV: Immediate Value
  //   D: Decode
  //   E: Execute
endmodule
