// Digital circuit 4bit_RegisterFile.dig as structural Verilog
module _4bit_RegisterFile (
  input  RR1,
  input  RR2,
  input  WR,
  input  [3:0] WD,
  input  K,
  input  WE,
  input  Clr,
  output [3:0] RD1,
  output [3:0] RD2
);

  wire and_1_out, and_2_out, not_1_out, not_2_out;
  wire [3:0] A_q, B_q, demultiplexer_1_out_0, demultiplexer_1_out_1, multiplexer_1_out, multiplexer_2_out;

  Demultiplexer #(.Bits(4)) demultiplexer_1 (
    .sel(WR), .in(WD), .out_0(demultiplexer_1_out_0), .out_1(demultiplexer_1_out_1));
  and and_1 (and_1_out, not_1_out, WE);
  not not_1 (not_1_out, WR);
  and and_2 (and_2_out, WR, WE);
  not not_2 (not_2_out, WE);
  Multiplexer #(.Bits(4)) multiplexer_1 (
    .sel(and_1_out), .in_0(A_q), .in_1(demultiplexer_1_out_0), .out(multiplexer_1_out));
  Multiplexer #(.Bits(4)) multiplexer_2 (
    .sel(and_2_out), .in_0(B_q), .in_1(demultiplexer_1_out_1), .out(multiplexer_2_out));
  _4bit_register A (.In(multiplexer_1_out), .K(K), .Clr(Clr), .Load(not_2_out), .Q(A_q));  // open: Q_2
  _4bit_register B (.In(multiplexer_2_out), .K(K), .Clr(Clr), .Load(not_2_out), .Q(B_q));  // open: Q_2
  Multiplexer #(.Bits(4)) multiplexer_3 (.sel(RR1), .in_0(A_q), .in_1(B_q), .out(RD1));
  Multiplexer #(.Bits(4)) multiplexer_4 (.sel(RR2), .in_0(A_q), .in_1(B_q), .out(RD2));

  // Notes on the sheet:
  //   RR1: Read Register 1
  //   select whether register A or B should be read
  //   RR2: Read Register 2
  //   select whether register A or B should be read
  //   WR: Write Register
  //   WD: Write Data
  //   RD1: Read Data 1
  //   RD2: Read Data 2
  //   WE: Write Enable
endmodule
