// Digital circuit 4bit_adder.dig as structural Verilog
module _4bit_adder (
  input  C_i__1,
  input  [3:0] A,
  input  [3:0] B,
  output C,
  output [3:0] sum
);

  wire _2_0_cout, _2_1_cout, _2_2_cout;

  _1bit_full_adder _2_0 (.A(A[0]), .B(B[0]), .Cin(C_i__1), .Sum(sum[0]), .Cout(_2_0_cout));
  _1bit_full_adder _2_1 (.A(A[1]), .B(B[1]), .Cin(_2_0_cout), .Sum(sum[1]), .Cout(_2_1_cout));
  _1bit_full_adder _2_2 (.A(A[2]), .B(B[2]), .Cin(_2_1_cout), .Sum(sum[2]), .Cout(_2_2_cout));
  _1bit_full_adder _2_3 (.A(A[3]), .B(B[3]), .Cin(_2_2_cout), .Sum(sum[3]), .Cout(C));

  // Notes on the sheet:
  //   A: input bus
  //   B: input bus
endmodule
