// Digital circuit CU_ALUInstructionMapper.dig as structural Verilog
module CU_ALUInstructionMapper (
  input  [3:0] opcode,
  output [2:0] Opp
);

  CU_IMZbit _2_0 (.A(opcode[3]), .B(opcode[2]), .C(opcode[1]), .D(opcode[0]), .Z(Opp[0]));
  CU_IMYbit _2_1 (.A(opcode[3]), .B(opcode[2]), .C(opcode[1]), .D(opcode[0]), .Y(Opp[1]));
  CU_IMXbit _2_2 (.A(opcode[3]), .B(opcode[2]), .C(opcode[1]), .D(opcode[0]), .X(Opp[2]));
endmodule
