// Digital circuit FDE_Cycle.dig as structural Verilog
module FDE_Cycle (
  input  In,
  input  K,
  output F,
  output D,
  output E
);

  wire A_q, and_1_out, and_2_out, and_3_out, and_4_out, B_q, not_1_out, not_2_out, not_3_out, not_4_out,
       not_5_out, not_6_out, not_7_out, not_8_out, not_9_out, not_10_out, not_11_out, or_1_out, or_2_out;

  D_FF A (.D(or_1_out), .C(K), .Q(A_q));  // open: nQ
  D_FF B (.D(or_2_out), .C(K), .Q(B_q));  // open: nQ
  and and_1 (and_1_out, A_q, not_1_out, not_2_out);
  not not_1 (not_1_out, B_q);
  not not_2 (not_2_out, In);
  and and_2 (and_2_out, not_3_out, B_q, In);
  not not_3 (not_3_out, A_q);
  and and_3 (and_3_out, not_4_out, not_5_out, In);
  not not_4 (not_4_out, A_q);
  not not_5 (not_5_out, B_q);
  and and_4 (and_4_out, not_6_out, B_q, not_7_out);
  not not_6 (not_6_out, A_q);
  not not_7 (not_7_out, In);
  or or_1 (or_1_out, and_1_out, and_2_out);
  or or_2 (or_2_out, and_3_out, and_4_out);
  not not_8 (not_8_out, or_1_out);
  not not_9 (not_9_out, or_2_out);
  not not_10 (not_10_out, or_1_out);
  not not_11 (not_11_out, or_2_out);
  and and_5 (F, not_8_out, not_9_out);
  and and_6 (D, not_10_out, or_2_out);
  and and_7 (E, or_1_out, not_11_out);
endmodule
