// Digital circuit Read_Register1.dig as structural Verilog
module Read_Register1 (
  input  [3:0] opcode,
  output read_reg_1
);

  wire not_1_out;

  not not_1 (not_1_out, opcode[3]);
  and and_1 (read_reg_1, opcode[0], opcode[1], opcode[2], not_1_out);

  // Notes on the sheet:
  //   read_reg_1: ! when B is read, 0 when A is read, also 0 when we don't care
endmodule
