// Digital circuit Read_Register2.dig as structural Verilog
module Read_Register2 (
  input  [3:0] opcode,
  output read_reg_2
);

  wire and_1_out, and_2_out, not_1_out;

  not not_1 (not_1_out, opcode[1]);
  and and_1 (and_1_out, opcode[1], opcode[3]);
  and and_2 (and_2_out, not_1_out, opcode[3]);
  or or_1 (read_reg_2, and_1_out, and_2_out);

  // Notes on the sheet:
  //   read_reg_2: 1 when B is read, 0 when A is read, 0 when we don't care
endmodule
