// Digital circuit SLT.dig as structural Verilog
module SLT (
  input  [3:0] A,
  input  [3:0] B,
  output SLT_flag
);

  wire _4bit_adder_subractor_1_c;

  _4bit_adder_subractor _4bit_adder_subractor_1 (.K(1'b1), .A(A), .B(B), .C(_4bit_adder_subractor_1_c));  // open: sum
  not not_1 (SLT_flag, _4bit_adder_subractor_1_c);

  // Notes on the sheet:
  //   SLT_flag: 1 if A < B
endmodule
