// Digital circuit Write_Enable.dig as structural Verilog
module Write_Enable (
  input  [3:0] opcode,
  output write_enable
);

  wire and_1_out, and_2_out, and_3_out, and_4_out, not_1_out, not_2_out, not_3_out, not_4_out;

  not not_1 (not_1_out, opcode[1]);
  not not_2 (not_2_out, opcode[3]);
  not not_3 (not_3_out, opcode[0]);
  not not_4 (not_4_out, opcode[3]);
  and and_1 (and_1_out, not_1_out, opcode[3]);
  and and_2 (and_2_out, opcode[0], not_2_out);
  and and_3 (and_3_out, opcode[1], opcode[3]);
  and and_4 (and_4_out, not_3_out, opcode[1], not_4_out);
  or or_1 (write_enable, and_1_out, and_2_out, and_3_out, and_4_out);

  // Notes on the sheet:
  //   write_enable: 1 when enabled, 0 when disabled, 1 or 0 when we don't care
endmodule
