// Digital circuit Write_Register.dig as structural Verilog
module Write_Register (
  input  [3:0] opcode,
  output write_reg
);

  wire and_1_out, and_2_out, not_1_out, not_2_out, not_3_out, not_4_out, not_5_out, not_6_out;

  not not_1 (not_1_out, opcode[0]);
  not not_2 (not_2_out, opcode[2]);
  not not_3 (not_3_out, opcode[3]);
  not not_4 (not_4_out, opcode[0]);
  not not_5 (not_5_out, opcode[1]);
  not not_6 (not_6_out, opcode[2]);
  and and_1 (and_1_out, not_1_out, opcode[1], not_2_out, not_3_out);
  and and_2 (and_2_out, not_4_out, not_5_out, not_6_out, opcode[3]);
  or or_1 (write_reg, and_1_out, and_2_out);

  // Notes on the sheet:
  //   write_reg: 1 when B is read, 0 when A is read, 0 when we don't care
endmodule
